# Fritzing sketch gardmon (saved by Fritzing 0.9.3b)
breadboards: 1

parts:
  DHT1 = DHT22 Humidity and Temperature Sensor
  ZS-042_RTC1 = ZS-042 RTC Module
  R1 = Resistor [tolerance=±5% resistance=100k package=THT]
  U1 = mystery part, 16 pins [chip_label=DMD]
  WeMos_D1_R1 = WeMos D1 R2
  R2 = Resistor [tolerance=±5% resistance=10k package=THT]
  Power_plug1 = Power plug
  U2 = mystery part, 4 pins [chip_label="5V Convertor"]

nets:
  VDD: DHT1.VDD, ZS-042_RTC1.VCC, R1.Pin_0, WeMos_D1_R1.3.3V
  N1: DHT1.DATA, R1.Pin_1, WeMos_D1_R1.D9
  GND: DHT1.GND, ZS-042_RTC1.GND, U1.pin2, U1.pin3, U1.pin4, U1.pin5, U1.pin6, U1.pin7, U1.pin8, WeMos_D1_R1.GND
  N2: ZS-042_RTC1.SDA, WeMos_D1_R1.D4
  N3: ZS-042_RTC1.SCL, WeMos_D1_R1.D3
  N4: U1.pin1, WeMos_D1_R1.D8, R2.Pin_0
  N5: U1.pin11, WeMos_D1_R1.(D7)
  N6: U1.pin12, WeMos_D1_R1.D10
  N7: U1.pin13, WeMos_D1_R1.(D5)
  N8: U1.pin15, WeMos_D1_R1.(D6)
  N9: U1.pin16, WeMos_D1_R1.D1/TX, WeMos_D1_R1.D2
  VIN: WeMos_D1_R1.VIN, Power_plug1.VCC, U2.pin1
  N10: R2.Pin_1, U2.pin4
  N11: Power_plug1.GND, U2.pin2

custom parts:
  WeMos D1 R2: The D1 R2 is a mini wifi board based on the ESP-8266EX.
